// Logisim project Projet.circ as structural Verilog: 8 circuits, main circuit main
module main (
  input  Do,
  input  Re,
  input  Mi,
  input  Fa,
  input  Sol,
  input  La,
  input  Si,
  output Argent,
  output Glace_Choco,
  output Glace_Vanille,
  output Coulis_Choco,
  output Coulis_Caramel,
  output Chantilly,
  output Smarties
);

  A A (.Do(Do), .Re(Re), .Mi(Mi), .Fa(Fa), .Sol(Sol), .La(La), .Si(Si), .S(Argent));
  GC GC (.Do(Do), .Re(Re), .Mi(Mi), .Fa(Fa), .Sol(Sol), .La(La), .Si(Si), .S(Glace_Choco));
  GV GV (.Do(Do), .Re(Re), .Mi(Mi), .Fa(Fa), .Sol(Sol), .La(La), .Si(Si), .S(Glace_Vanille));
  CC CC (.Do(Do), .Re(Re), .Mi(Mi), .Fa(Fa), .Sol(Sol), .La(La), .Si(Si), .S(Coulis_Choco));
  CCa CCa (.Do(Do), .Re(Re), .Mi(Mi), .Fa(Fa), .Sol(Sol), .La(La), .Si(Si), .S(Coulis_Caramel));
  Ch Ch (.Do(Do), .Re(Re), .Mi(Mi), .Fa(Fa), .Sol(Sol), .La(La), .Si(Si), .S(Chantilly));
  S S (.Do(Do), .Re(Re), .Mi(Mi), .Fa(Fa), .Sol(Sol), .La(La), .Si(Si), .S(Smarties));
endmodule

module S (
  input  Do,
  input  Re,
  input  Mi,
  input  Fa,
  input  Sol,
  input  La,
  input  Si,
  output S
);

  wire and_1_out, and_2_out, or_1_out, xor_1_out, xor_2_out;

  xor xor_1 (xor_1_out, Re, Mi);
  and and_1 (and_1_out, xor_1_out, xor_2_out);
  xor xor_2 (xor_2_out, Fa, Sol);
  and and_2 (and_2_out, Re, Mi, ~Fa, ~Sol);  // AND_Gate
  or or_1 (or_1_out, and_1_out, and_2_out);
  and and_3 (S, Do, or_1_out, ~La, Si);  // AND_Gate
endmodule

module Ch (
  input  Do,
  input  Re,
  input  Mi,
  input  Fa,
  input  Sol,
  input  La,
  input  Si,
  output S
);

  wire and_1_out, and_2_out, or_1_out, xor_1_out, xor_2_out;

  xor xor_1 (xor_1_out, Re, Mi);
  and and_1 (and_1_out, xor_1_out, xor_2_out);
  xor xor_2 (xor_2_out, Fa, Sol);
  and and_2 (and_2_out, Re, Mi, ~Fa, ~Sol);  // AND_Gate
  or or_1 (or_1_out, and_1_out, and_2_out);
  and and_3 (S, Do, or_1_out, La, ~Si);  // AND_Gate
endmodule

module CC (
  input  Do,
  input  Re,
  input  Mi,
  input  Fa,
  input  Sol,
  input  La,
  input  Si,
  output S
);

  wire and_1_out, and_2_out, or_1_out, xor_1_out, xor_2_out;

  xor xor_1 (xor_1_out, Re, Mi);
  and and_1 (and_1_out, xor_1_out, xor_2_out);
  xor xor_2 (xor_2_out, La, Si);
  and and_2 (and_2_out, Mi, Re, ~La, ~Si);  // AND_Gate
  or or_1 (or_1_out, and_1_out, and_2_out);
  and and_3 (S, Do, Fa, ~Sol, or_1_out);  // AND_Gate
endmodule

module GC (
  input  Do,
  input  Re,
  input  Mi,
  input  Fa,
  input  Sol,
  input  La,
  input  Si,
  output S
);

  wire and_1_out, and_2_out, or_1_out, xor_1_out, xor_2_out, xor_3_out;

  xor xor_1 (xor_1_out, Fa, Sol);
  xor xor_2 (xor_2_out, La, Si);
  xor xor_3 (xor_3_out, xor_1_out, xor_2_out);
  and and_1 (and_1_out, Mi, xor_3_out);
  and and_2 (and_2_out, ~Mi, xor_1_out, xor_2_out);  // AND_Gate
  or or_1 (or_1_out, and_2_out, and_1_out);
  and and_3 (S, Do, Re, or_1_out);
endmodule

module GV (
  input  Do,
  input  Re,
  input  Mi,
  input  Fa,
  input  Sol,
  input  La,
  input  Si,
  output S
);

  wire and_1_out, and_2_out, or_1_out, xor_1_out, xor_2_out, xor_3_out;

  xor xor_1 (xor_1_out, Fa, Sol);
  xor xor_2 (xor_2_out, La, Si);
  xor xor_3 (xor_3_out, xor_1_out, xor_2_out);
  and and_1 (and_1_out, Re, xor_3_out);
  and and_2 (and_2_out, ~Re, xor_1_out, xor_2_out);  // AND_Gate
  or or_1 (or_1_out, and_2_out, and_1_out);
  and and_3 (S, Do, Mi, or_1_out);
endmodule

module CCa (
  input  Do,
  input  Re,
  input  Mi,
  input  Fa,
  input  Sol,
  input  La,
  input  Si,
  output S
);

  wire and_1_out, and_2_out, or_1_out, xor_1_out, xor_2_out;

  xor xor_1 (xor_1_out, Re, Mi);
  and and_1 (and_1_out, xor_1_out, xor_2_out);
  xor xor_2 (xor_2_out, La, Si);
  and and_2 (and_2_out, Mi, Re, ~La, ~Si);  // AND_Gate
  or or_1 (or_1_out, and_1_out, and_2_out);
  and and_3 (S, Do, ~Fa, Sol, or_1_out);  // AND_Gate
endmodule

module A (
  input  Do,
  input  Re,
  input  Mi,
  input  Fa,
  input  Sol,
  input  La,
  input  Si,
  output S
);

  wire and_1_out, and_2_out, and_3_out, and_4_out, and_5_out, and_6_out, or_1_out, xor_1_out, xor_2_out,
       xor_3_out, xor_4_out;

  xor xor_1 (xor_1_out, Si, La);
  xor xor_2 (xor_2_out, Sol, Fa);
  xor xor_3 (xor_3_out, Mi, Re);
  xor xor_4 (xor_4_out, xor_1_out, xor_2_out);
  and and_1 (and_1_out, xor_4_out, xor_3_out);
  and and_2 (and_2_out, xor_1_out, xor_2_out, Re, Mi);
  and and_3 (and_3_out, ~Re, ~Mi);  // AND_Gate
  and and_4 (and_4_out, Fa, Sol);
  and and_5 (and_5_out, La, Si);
  and and_6 (and_6_out, ~Si, ~La, ~Sol, ~Fa);  // AND_Gate
  or or_1 (or_1_out, and_3_out, and_4_out, and_6_out, and_1_out, and_2_out, and_5_out);
  and and_7 (S, Do, or_1_out);
endmodule
